// Digital circuit ALU.dig as structural Verilog
module ALU (
  input  [15:0] Left,
  input  [15:0] Right,
  input  [1:0] ALUOp,
  output [15:0] result,
  output greater,
  output eq,
  output less
);

  wire [15:0] add_1_s, and_1_out, neg_1_out, or_1_out;

  Add #(.Bits(16)) add_1 (.a(Left), .b(Right), .c_i(1'b0), .s(add_1_s));  // open: c_o
  assign and_1_out = Left & Right;  // And and_1, 16 bits wide
  assign or_1_out = Left | Right;  // Or or_1, 16 bits wide
  Neg #(.Bits(16)) neg_1 (.in(Left), .out(neg_1_out));
  Comparator #(.Bits(16)) comparator_1 (.a(Left), .b(Right), .gt(greater), .eq(eq), .lt(less));
  Multiplexer #(.Bits(16), .Selector_Bits(2)) multiplexer_1 (
    .sel(ALUOp), .in_0(add_1_s), .in_1(and_1_out), .in_2(or_1_out), .in_3(neg_1_out), .out(result));
endmodule
