// Digital circuit Branch-Unit.dig as structural Verilog
module Branch_Unit (
  input  greater,
  input  eq,
  input  less,
  input  [3:0] Opcode,
  output Branch
);

  wire and_1_out, and_2_out, and_3_out, and_4_out, and_5_out, and_6_out, and_7_out, and_8_out, not_1_out,
       not_2_out, not_3_out, not_4_out, not_5_out, not_6_out, not_7_out, not_8_out, not_9_out;

  not not_1 (not_1_out, Opcode[1]);
  not not_2 (not_2_out, Opcode[3]);
  not not_3 (not_3_out, Opcode[0]);
  not not_4 (not_4_out, Opcode[3]);
  not not_5 (not_5_out, Opcode[3]);
  not not_6 (not_6_out, Opcode[0]);
  not not_7 (not_7_out, Opcode[1]);
  not not_8 (not_8_out, Opcode[2]);
  and and_1 (and_1_out, Opcode[0], not_1_out, Opcode[2], not_2_out);
  and and_2 (and_2_out, not_3_out, Opcode[1], Opcode[2], not_4_out);
  and and_3 (and_3_out, Opcode[0], Opcode[1], Opcode[2], not_5_out);
  and and_4 (and_4_out, not_6_out, not_7_out, not_8_out, Opcode[3]);
  not not_9 (not_9_out, eq);
  and and_5 (and_5_out, eq, and_1_out);
  and and_6 (and_6_out, not_9_out, and_2_out);
  and and_7 (and_7_out, less, and_3_out);
  and and_8 (and_8_out, greater, and_4_out);
  or or_1 (Branch, and_5_out, and_6_out, and_7_out, and_8_out);

  // Notes on the sheet:
  //   This component decides whether to branch or not.
  //   beq
  //   bne
  //   blt
  //   bgt
endmodule
