// Digital circuit Decoder.dig as structural Verilog
module Decoder (
  input  [15:0] instruction,
  output [3:0] opcode,
  output [1:0] rs,
  output [1:0] rt,
  output [7:0] immediate_8,
  output [11:0] address
);

  // Pins of 1 and 12 bits meet at instruction[11:0]

  assign address = instruction[11:0];
  assign immediate_8 = instruction[7:0];
  assign opcode = instruction[15:12];
  assign rs = instruction[11:10];
  assign rt = instruction[9:8];
endmodule
