// Digital circuit Program Counter.dig as structural Verilog
module Program_Counter (
  input  [15:0] address_i,
  input  [15:0] write,
  input  CLK,
  output [15:0] address_o
);

  CounterPreset #(.Bits(16)) counterpreset_1 (
    .en(1'b1), .C(CLK), .dir(1'b0), .in(address_i), .ld(write[0]), .clr(1'b0), .out(address_o));  // open: ovf
  // Pins of 1 and 16 bits meet at write
endmodule
