// Digital circuit Program Memory.dig as structural Verilog
module Program_Memory (
  input  [3:0] address,
  output [15:0] instruction
);

  EEPROMDualPort #(.AddrBits(4), .isProgramMemory("true"), .Bits(16)) \program  (
    .A(address), .Din({16{1'b0}}), .str(1'b0), .C(1'b0), .ld(1'b1), .D(instruction));

  // Notes on the sheet:
  //   contents of program (hex, n*v repeats v):
  //   6106,1007,1002,4c0,0,4000,5*0,4001
endmodule
