// Digital circuit RAM.dig as structural Verilog
module RAM (
  input  CLK
);

  RAMDualPort ramdualport_1 ();  // open: A, Din, str, C, ld, D
  BlockRAMDualPort blockramdualport_1 ();  // open: A, Din, str, C, D
  RAMSinglePort ramsingleport_1 ();  // open: A, str, C, ld, D
  RAMDualAccess ramdualaccess_1 ();  // open: str, C, ld, A1, Din1, A2, D1, D2
  GraphicCard graphiccard_1 ();  // open: A, str, C, ld, B, D
endmodule
