// Digital circuit Register File.dig as structural Verilog
module Register_File (
  input  [1:0] Reg_1_Read,
  input  [1:0] Reg_2_Read,
  input  [1:0] Reg_Write,
  input  [15:0] data,
  input  CLK,
  input  Write_Enable,
  output [15:0] Reg_1_Value,
  output [15:0] Reg_2_Value,
  output [15:0] R1,
  output [15:0] R2,
  output [15:0] R3,
  output [15:0] R4
);

  wire demultiplexer_1_out_0, demultiplexer_1_out_1, demultiplexer_1_out_2, demultiplexer_1_out_3;

  Demultiplexer #(.Selector_Bits(2)) demultiplexer_1 (
    .sel(Reg_Write), .in(Write_Enable), .out_0(demultiplexer_1_out_0), .out_1(demultiplexer_1_out_1),
    .out_2(demultiplexer_1_out_2), .out_3(demultiplexer_1_out_3));
  Register #(.Bits(16)) u_R1 (.D(data), .C(CLK), .en(demultiplexer_1_out_0), .Q(R1));
  Register #(.Bits(16)) u_R2 (.D(data), .C(CLK), .en(demultiplexer_1_out_1), .Q(R2));
  Register #(.Bits(16)) u_R3 (.D(data), .C(CLK), .en(demultiplexer_1_out_2), .Q(R3));
  Register #(.Bits(16)) u_R4 (.D(data), .C(CLK), .en(demultiplexer_1_out_3), .Q(R4));
  Multiplexer #(.Selector_Bits(2), .Bits(16)) multiplexer_1 (
    .sel(Reg_1_Read), .in_0(R1), .in_1(R2), .in_2(R3), .in_3(R4), .out(Reg_1_Value));
  Multiplexer #(.Selector_Bits(2), .Bits(16)) multiplexer_2 (
    .sel(Reg_2_Read), .in_0(R1), .in_1(R2), .in_2(R3), .in_3(R4), .out(Reg_2_Value));
endmodule
