// Digital circuit display_driver_inst_1.dig as structural Verilog
module display_driver_inst_1 (
  input  [3:0] Opcode,
  output [15:0] D1,
  output P1,
  output [15:0] D2,
  output P2,
  output [15:0] D3,
  output P3,
  output [15:0] D4,
  output P4,
  output [15:0] D5,
  output P5
);

  ROM #(.AddrBits(4), .Bits(16)) rom_1 (.A(Opcode), .sel(1'b1), .D(D1));
  ROM #(.AddrBits(4), .Bits(16)) rom_2 (.A(Opcode), .sel(1'b1), .D(D2));
  ROM #(.AddrBits(4), .Bits(16)) rom_3 (.A(Opcode), .sel(1'b1), .D(D3));
  ROM #(.AddrBits(4), .Bits(16)) rom_4 (.A(Opcode), .sel(1'b1), .D(D4));
  ROM #(.AddrBits(4), .Bits(16)) rom_5 (.A(Opcode), .sel(1'b1), .D(D5));

  assign P1 = 1'b0;
  assign P2 = 1'b0;
  assign P3 = 1'b0;
  assign P4 = 1'b0;
  assign P5 = 1'b0;
endmodule
