// Digital circuit display_driver_reg.dig as structural Verilog
module display_driver_reg (
  input  [3:0] Opcode,
  output [3:0] D1,
  output P1,
  output [3:0] D2,
  output P2
);

  ROM #(.AddrBits(4), .Bits(4)) rom_1 (.A(Opcode), .sel(1'b1), .D(D1));
  ROM #(.AddrBits(4), .Bits(4)) rom_2 (.A(Opcode), .sel(1'b1), .D(D2));

  assign P1 = 1'b0;
  assign P2 = 1'b0;
endmodule
